# Fritzing sketch DHT11 (saved by Fritzing 0.9.4)
breadboards: 1

parts:
  RHT1 = Humidity and Temperature Sensor RHT03
  Part1 = Arduino Uno (Rev3)
  R1 = Resistor [tolerance=±5% resistance=4.7k package=THT]

nets:
  VCC: RHT1.Vcc, Part1.5V, R1.Pin_0
  N1: RHT1.Data-signal, Part1.D2, R1.Pin_1
  N2: RHT1.GND_2, Part1.GND
